// Logisim project Clock.circ as structural Verilog: 1 circuit, main circuit main
module main (
);

  wire and_1_out, and_2_out, and_3_out, and_4_out, and_5_out, and_6_out, and_7_out, and_8_out, and_9_out,
       and_10_out, and_11_out, and_12_out, and_13_out, and_14_out, and_15_out, and_16_out, and_17_out,
       and_18_out, and_19_out, and_20_out, and_21_out, and_22_out, and_23_out, and_24_out, and_25_out,
       and_26_out, and_27_out, and_28_out, and_29_out, and_30_out, clock_1_out, or_1_out, or_2_out, or_3_out,
       or_4_out, or_5_out, or_6_out, or_7_out, or_8_out, or_9_out, t_ff_1_q, t_ff_1_qn, t_ff_2_q, t_ff_2_qn,
       t_ff_3_q, t_ff_3_qn, t_ff_4_q, t_ff_4_qn;

  Clock clock_1 (.out(clock_1_out));
  or or_1 (or_1_out, and_2_out, and_1_out);
  and and_1 (and_1_out, t_ff_1_qn, t_ff_2_q, t_ff_3_q, t_ff_4_q);
  and and_2 (and_2_out, t_ff_1_q, t_ff_2_qn, t_ff_3_qn, t_ff_4_q);
  LED led_1 (.in(t_ff_1_q));
  T_Flip_Flop #(.trigger("falling")) t_ff_1 (
    .clk(clock_1_out), .T(or_1_out), .Q(t_ff_1_q), .Qn(t_ff_1_qn), .en(1'b1));  // open: preset, reset
  T_Flip_Flop #(.trigger("falling")) t_ff_2 (
    .clk(clock_1_out), .T(and_3_out), .Q(t_ff_2_q), .Qn(t_ff_2_qn), .en(1'b1));  // open: preset, reset
  and and_3 (and_3_out, t_ff_1_qn, t_ff_3_q, t_ff_4_q);
  LED led_2 (.in(t_ff_2_q));
  T_Flip_Flop #(.trigger("falling")) t_ff_3 (
    .clk(clock_1_out), .T(and_4_out), .Q(t_ff_3_q), .Qn(t_ff_3_qn), .en(1'b1));  // open: preset, reset
  and and_4 (and_4_out, t_ff_1_qn, t_ff_4_q);
  LED led_3 (.in(t_ff_3_q));
  T_Flip_Flop #(.trigger("falling")) t_ff_4 (
    .clk(clock_1_out), .T(or_2_out), .Q(t_ff_4_q), .Qn(t_ff_4_qn), .en(1'b1));  // open: preset, reset
  or or_2 (or_2_out, t_ff_1_qn, and_5_out);
  and and_5 (and_5_out, t_ff_2_qn, t_ff_3_qn);
  and and_6 (and_6_out, t_ff_2_qn, t_ff_3_qn, t_ff_4_qn);
  and and_7 (and_7_out, t_ff_1_qn, t_ff_2_qn, t_ff_3_q, t_ff_4_q);
  and and_8 (and_8_out, t_ff_1_qn, t_ff_2_q, t_ff_3_qn, t_ff_4_q);
  and and_9 (and_9_out, t_ff_1_qn, t_ff_2_q, t_ff_3_q, t_ff_4_qn);
  and and_10 (and_10_out, t_ff_1_q, t_ff_2_qn, t_ff_3_qn);
  and and_11 (and_11_out, t_ff_1_qn, t_ff_3_q, t_ff_4_qn);
  and and_12 (and_12_out, t_ff_2_qn, t_ff_3_qn, t_ff_4_qn);
  LED led_4 (.in(t_ff_4_q));
  or or_3 (or_3_out, and_11_out, and_12_out);
  and and_13 (and_13_out, t_ff_1_qn, t_ff_2_q, t_ff_4_q);
  and and_14 (and_14_out, t_ff_1_q, t_ff_2_qn, t_ff_3_qn);
  and and_15 (and_15_out, t_ff_1_qn, t_ff_2_qn, t_ff_4_qn);
  and and_16 (and_16_out, t_ff_1_qn, t_ff_2_qn);
  and and_17 (and_17_out, t_ff_1_qn, t_ff_3_qn, t_ff_4_qn);
  and and_18 (and_18_out, t_ff_1_qn, t_ff_3_q, t_ff_4_q);
  and and_19 (and_19_out, t_ff_2_qn, t_ff_3_qn);
  and and_20 (and_20_out, t_ff_1_qn, t_ff_4_q);
  and and_21 (and_21_out, t_ff_1_qn, t_ff_2_q);
  and and_22 (and_22_out, t_ff_2_qn, t_ff_3_qn);
  and and_23 (and_23_out, t_ff_1_qn, t_ff_3_q);
  or or_4 (or_4_out, and_20_out, and_21_out, and_22_out);
  and and_24 (and_24_out, t_ff_1_qn, t_ff_4_qn);
  and and_25 (and_25_out, t_ff_1_qn, t_ff_2_q, t_ff_3_qn);
  and and_26 (and_26_out, t_ff_1_q, t_ff_2_qn, t_ff_3_qn);
  and and_27 (and_27_out, t_ff_1_qn, t_ff_2_qn, t_ff_3_q, t_ff_4_q);
  and and_28 (and_28_out, t_ff_1_qn, t_ff_2_q, t_ff_3_qn);
  and and_29 (and_29_out, t_ff_1_qn, t_ff_2_q, t_ff_4_qn);
  and and_30 (and_30_out, t_ff_3_qn, t_ff_2_qn, t_ff_1_q);
  or or_5 (or_5_out, and_23_out, and_13_out, and_14_out, and_15_out);
  or or_6 (or_6_out, and_16_out, and_17_out, and_18_out, and_19_out);
  or or_7 (or_7_out, and_6_out, and_7_out, and_8_out, and_9_out, and_10_out);
  or or_8 (or_8_out, and_24_out, and_25_out, and_26_out);
  or or_9 (or_9_out, and_27_out, and_28_out, and_29_out, and_30_out);
  _7_Segment_Display u_7_segment_display_1 (
    .g(or_9_out), .f(or_8_out), .a(or_5_out), .b(or_6_out), .e(or_3_out), .d(or_7_out), .c(or_4_out));  // open: dp

  // Notes on the sheet:
  //   A
  //   B
  //   C
  //   D
endmodule
