// Logisim project Clock2.circ as structural Verilog: 1 circuit, main circuit main
module main (
);

  wire and_1_out, and_2_out, and_3_out, and_4_out, and_5_out, and_6_out, and_7_out, and_8_out, and_9_out,
       clock_1_out, n7_segment_display_driver_1_p6, n7_segment_display_driver_1_p7,
       n7_segment_display_driver_1_p8, n7_segment_display_driver_1_p9, n7_segment_display_driver_1_p10,
       n7_segment_display_driver_1_p11, n7_segment_display_driver_1_p12, n7_segment_display_driver_2_p8,
       n7_segment_display_driver_2_p9, n7_segment_display_driver_2_p10, n7_segment_display_driver_2_p11,
       n7_segment_display_driver_2_p12, n7_segment_display_driver_2_p13, n7_segment_display_driver_2_p14,
       not_1_out, or_1_out, or_2_out, or_3_out, or_4_out, t_ff_1_q, t_ff_1_qn, t_ff_2_q, t_ff_2_qn, t_ff_3_q,
       t_ff_3_qn, t_ff_4_q, t_ff_4_qn, t_ff_5_q, t_ff_5_qn, t_ff_6_q, t_ff_6_qn, t_ff_7_q, t_ff_7_qn;

  Clock clock_1 (.out(clock_1_out));
  T_Flip_Flop #(.trigger("falling")) t_ff_1 (
    .clk(and_2_out), .T(or_1_out), .Q(t_ff_1_q), .Qn(t_ff_1_qn), .en(1'b1));  // open: preset, reset
  T_Flip_Flop #(.trigger("falling")) t_ff_2 (
    .clk(and_2_out), .T(and_5_out), .Q(t_ff_2_q), .Qn(t_ff_2_qn), .en(1'b1));  // open: preset, reset
  T_Flip_Flop #(.trigger("falling")) t_ff_3 (
    .clk(and_2_out), .T(or_3_out), .Q(t_ff_3_q), .Qn(t_ff_3_qn), .en(1'b1));  // open: preset, reset
  and and_1 (and_1_out, t_ff_1_q, t_ff_2_qn, t_ff_3_q);
  or or_1 (or_1_out, and_1_out, and_4_out);
  and and_2 (and_2_out, t_ff_7_q, t_ff_6_qn, t_ff_5_qn, t_ff_4_q);
  T_Flip_Flop #(.trigger("falling")) t_ff_4 (
    .clk(clock_1_out), .T(or_2_out), .Q(t_ff_4_q), .Qn(t_ff_4_qn), .en(1'b1));  // open: preset, reset
  T_Flip_Flop #(.trigger("falling")) t_ff_5 (
    .clk(clock_1_out), .T(and_8_out), .Q(t_ff_5_q), .Qn(t_ff_5_qn), .en(1'b1));  // open: preset, reset
  T_Flip_Flop #(.trigger("falling")) t_ff_6 (
    .clk(clock_1_out), .T(and_7_out), .Q(t_ff_6_q), .Qn(t_ff_6_qn), .en(1'b1));  // open: preset, reset
  T_Flip_Flop #(.trigger("falling")) t_ff_7 (
    .clk(clock_1_out), .T(or_4_out), .Q(t_ff_7_q), .Qn(t_ff_7_qn), .en(1'b1));  // open: preset, reset
  and and_3 (and_3_out, t_ff_4_qn, t_ff_5_q, t_ff_6_q, t_ff_7_q);
  and and_4 (and_4_out, t_ff_1_qn, t_ff_2_q, t_ff_3_q);
  and and_5 (and_5_out, t_ff_1_qn, t_ff_3_q);
  and and_6 (and_6_out, t_ff_4_q, t_ff_5_qn, t_ff_6_qn, t_ff_7_q);
  or or_2 (or_2_out, and_3_out, and_6_out);
  not not_1 (not_1_out, 1'b1);
  or or_3 (or_3_out, t_ff_1_qn, t_ff_2_qn);
  and and_7 (and_7_out, t_ff_4_qn, t_ff_7_q);
  and and_8 (and_8_out, t_ff_4_qn, t_ff_6_q, t_ff_7_q);
  and and_9 (and_9_out, t_ff_5_qn, t_ff_6_qn);
  or or_4 (or_4_out, t_ff_4_qn, and_9_out);
  // _7_segment_display_driver 7_segment_display_driver_1: pin names not known; wires that end beside it: t_ff_7_qn, t_ff_4_q, t_ff_5_q, t_ff_6_q, t_ff_7_q, n7_segment_display_driver_1_p6, n7_segment_display_driver_1_p7, n7_segment_display_driver_1_p8, n7_segment_display_driver_1_p9, n7_segment_display_driver_1_p10, n7_segment_display_driver_1_p11, n7_segment_display_driver_1_p12
  // _7_segment_display_driver 7_segment_display_driver_2: pin names not known; wires that end beside it: t_ff_1_qn, t_ff_2_qn, t_ff_3_qn, not_1_out, t_ff_1_q, t_ff_2_q, t_ff_3_q, n7_segment_display_driver_2_p8, n7_segment_display_driver_2_p9, n7_segment_display_driver_2_p10, n7_segment_display_driver_2_p11, n7_segment_display_driver_2_p12, n7_segment_display_driver_2_p13, n7_segment_display_driver_2_p14
  _7_Segment_Display u_7_segment_display_1 (
    .g(n7_segment_display_driver_2_p14), .f(n7_segment_display_driver_2_p13),
    .a(n7_segment_display_driver_2_p8), .b(n7_segment_display_driver_2_p9),
    .e(n7_segment_display_driver_2_p12), .d(n7_segment_display_driver_2_p11),
    .c(n7_segment_display_driver_2_p10));  // open: dp
  _7_Segment_Display u_7_segment_display_2 (
    .g(n7_segment_display_driver_1_p12), .f(n7_segment_display_driver_1_p11),
    .a(n7_segment_display_driver_1_p6), .b(n7_segment_display_driver_1_p7),
    .e(n7_segment_display_driver_1_p10), .d(n7_segment_display_driver_1_p9),
    .c(n7_segment_display_driver_1_p8));  // open: dp
endmodule
