// Logisim project Clock3.circ as structural Verilog: 1 circuit, main circuit main
module main (
);

  wire and_1_out, and_2_out, and_3_out, and_4_out, and_5_out, and_6_out, and_7_out, and_8_out, and_9_out,
       and_10_out, and_11_out, and_12_out, and_13_out, and_14_out, and_15_out, and_16_out, and_17_out,
       and_18_out, and_19_out, and_20_out, clock_1_out, n7_segment_display_driver_1_p8,
       n7_segment_display_driver_1_p9, n7_segment_display_driver_1_p10, n7_segment_display_driver_1_p11,
       n7_segment_display_driver_1_p12, n7_segment_display_driver_1_p13, n7_segment_display_driver_1_p14,
       n7_segment_display_driver_2_p6, n7_segment_display_driver_2_p7, n7_segment_display_driver_2_p8,
       n7_segment_display_driver_2_p9, n7_segment_display_driver_2_p10, n7_segment_display_driver_2_p11,
       n7_segment_display_driver_2_p12, n7_segment_display_driver_3_p8, n7_segment_display_driver_3_p9,
       n7_segment_display_driver_3_p10, n7_segment_display_driver_3_p11, n7_segment_display_driver_3_p12,
       n7_segment_display_driver_3_p13, n7_segment_display_driver_3_p14, n7_segment_display_driver_4_p6,
       n7_segment_display_driver_4_p7, n7_segment_display_driver_4_p8, n7_segment_display_driver_4_p9,
       n7_segment_display_driver_4_p10, n7_segment_display_driver_4_p11, n7_segment_display_driver_4_p12,
       not_1_out, not_2_out, or_1_out, or_2_out, or_3_out, or_4_out, or_5_out, or_6_out, or_7_out, or_8_out,
       t_ff_1_q, t_ff_1_qn, t_ff_2_q, t_ff_2_qn, t_ff_3_q, t_ff_3_qn, t_ff_4_q, t_ff_4_qn, t_ff_5_q,
       t_ff_5_qn, t_ff_6_q, t_ff_6_qn, t_ff_7_q, t_ff_7_qn, t_ff_8_q, t_ff_8_qn, t_ff_9_q, t_ff_9_qn,
       t_ff_10_q, t_ff_10_qn, t_ff_11_q, t_ff_11_qn, t_ff_12_q, t_ff_12_qn, t_ff_13_q, t_ff_13_qn, t_ff_14_q,
       t_ff_14_qn;

  T_Flip_Flop #(.trigger("falling")) t_ff_1 (
    .clk(and_1_out), .T(or_1_out), .Q(t_ff_1_q), .Qn(t_ff_1_qn), .en(1'b1));  // open: preset, reset
  T_Flip_Flop #(.trigger("falling")) t_ff_2 (
    .clk(and_1_out), .T(and_5_out), .Q(t_ff_2_q), .Qn(t_ff_2_qn), .en(1'b1));  // open: preset, reset
  T_Flip_Flop #(.trigger("falling")) t_ff_3 (
    .clk(and_1_out), .T(or_3_out), .Q(t_ff_3_q), .Qn(t_ff_3_qn), .en(1'b1));  // open: preset, reset
  and and_1 (and_1_out, t_ff_7_q, t_ff_6_qn, t_ff_5_qn, t_ff_4_q);
  T_Flip_Flop #(.trigger("falling")) t_ff_4 (
    .clk(and_10_out), .T(or_2_out), .Q(t_ff_4_q), .Qn(t_ff_4_qn), .en(1'b1));  // open: preset, reset
  T_Flip_Flop #(.trigger("falling")) t_ff_5 (
    .clk(and_10_out), .T(and_7_out), .Q(t_ff_5_q), .Qn(t_ff_5_qn), .en(1'b1));  // open: preset, reset
  T_Flip_Flop #(.trigger("falling")) t_ff_6 (
    .clk(and_10_out), .T(and_8_out), .Q(t_ff_6_q), .Qn(t_ff_6_qn), .en(1'b1));  // open: preset, reset
  T_Flip_Flop #(.trigger("falling")) t_ff_7 (
    .clk(and_10_out), .T(or_4_out), .Q(t_ff_7_q), .Qn(t_ff_7_qn), .en(1'b1));  // open: preset, reset
  and and_2 (and_2_out, t_ff_1_q, t_ff_2_qn, t_ff_3_q);
  and and_3 (and_3_out, t_ff_1_qn, t_ff_2_q, t_ff_3_q);
  or or_1 (or_1_out, and_2_out, and_3_out);
  and and_4 (and_4_out, t_ff_4_qn, t_ff_5_q, t_ff_6_q, t_ff_7_q);
  or or_2 (or_2_out, and_4_out, and_6_out);
  not not_1 (not_1_out, 1'b1);
  and and_5 (and_5_out, t_ff_1_qn, t_ff_3_q);
  or or_3 (or_3_out, t_ff_1_qn, t_ff_2_qn);
  and and_6 (and_6_out, t_ff_4_q, t_ff_5_qn, t_ff_6_qn, t_ff_7_q);
  and and_7 (and_7_out, t_ff_4_qn, t_ff_6_q, t_ff_7_q);
  or or_4 (or_4_out, t_ff_4_qn, and_9_out);
  and and_8 (and_8_out, t_ff_4_qn, t_ff_7_q);
  and and_9 (and_9_out, t_ff_5_qn, t_ff_6_qn);
  // _7_segment_display_driver 7_segment_display_driver_1: pin names not known; wires that end beside it: t_ff_1_qn, t_ff_2_qn, t_ff_3_qn, not_1_out, t_ff_1_q, t_ff_2_q, t_ff_3_q, n7_segment_display_driver_1_p8, n7_segment_display_driver_1_p9, n7_segment_display_driver_1_p10, n7_segment_display_driver_1_p11, n7_segment_display_driver_1_p12, n7_segment_display_driver_1_p13, n7_segment_display_driver_1_p14
  // _7_segment_display_driver 7_segment_display_driver_2: pin names not known; wires that end beside it: t_ff_7_qn, t_ff_4_q, t_ff_5_q, t_ff_6_q, t_ff_7_q, n7_segment_display_driver_2_p6, n7_segment_display_driver_2_p7, n7_segment_display_driver_2_p8, n7_segment_display_driver_2_p9, n7_segment_display_driver_2_p10, n7_segment_display_driver_2_p11, n7_segment_display_driver_2_p12
  _7_Segment_Display u_7_segment_display_1 (
    .g(n7_segment_display_driver_1_p14), .f(n7_segment_display_driver_1_p13),
    .a(n7_segment_display_driver_1_p8), .b(n7_segment_display_driver_1_p9),
    .e(n7_segment_display_driver_1_p12), .d(n7_segment_display_driver_1_p11),
    .c(n7_segment_display_driver_1_p10));  // open: dp
  _7_Segment_Display u_7_segment_display_2 (
    .g(n7_segment_display_driver_2_p12), .f(n7_segment_display_driver_2_p11),
    .a(n7_segment_display_driver_2_p6), .b(n7_segment_display_driver_2_p7),
    .e(n7_segment_display_driver_2_p10), .d(n7_segment_display_driver_2_p9),
    .c(n7_segment_display_driver_2_p8));  // open: dp
  and and_10 (and_10_out, and_11_out, and_12_out);
  Clock clock_1 (.out(clock_1_out));
  and and_11 (and_11_out, t_ff_10_q, t_ff_9_qn, t_ff_8_q);
  T_Flip_Flop #(.trigger("falling")) t_ff_8 (
    .clk(and_12_out), .T(or_5_out), .Q(t_ff_8_q), .Qn(t_ff_8_qn), .en(1'b1));  // open: preset, reset
  T_Flip_Flop #(.trigger("falling")) t_ff_9 (
    .clk(and_12_out), .T(and_16_out), .Q(t_ff_9_q), .Qn(t_ff_9_qn), .en(1'b1));  // open: preset, reset
  T_Flip_Flop #(.trigger("falling")) t_ff_10 (
    .clk(and_12_out), .T(or_7_out), .Q(t_ff_10_q), .Qn(t_ff_10_qn), .en(1'b1));  // open: preset, reset
  and and_12 (and_12_out, t_ff_14_q, t_ff_13_qn, t_ff_12_qn, t_ff_11_q);
  T_Flip_Flop #(.trigger("falling")) t_ff_11 (
    .clk(clock_1_out), .T(or_6_out), .Q(t_ff_11_q), .Qn(t_ff_11_qn), .en(1'b1));  // open: preset, reset
  T_Flip_Flop #(.trigger("falling")) t_ff_12 (
    .clk(clock_1_out), .T(and_18_out), .Q(t_ff_12_q), .Qn(t_ff_12_qn), .en(1'b1));  // open: preset, reset
  T_Flip_Flop #(.trigger("falling")) t_ff_13 (
    .clk(clock_1_out), .T(and_19_out), .Q(t_ff_13_q), .Qn(t_ff_13_qn), .en(1'b1));  // open: preset, reset
  T_Flip_Flop #(.trigger("falling")) t_ff_14 (
    .clk(clock_1_out), .T(or_8_out), .Q(t_ff_14_q), .Qn(t_ff_14_qn), .en(1'b1));  // open: preset, reset
  and and_13 (and_13_out, t_ff_8_q, t_ff_9_qn, t_ff_10_q);
  and and_14 (and_14_out, t_ff_8_qn, t_ff_9_q, t_ff_10_q);
  or or_5 (or_5_out, and_13_out, and_14_out);
  and and_15 (and_15_out, t_ff_11_qn, t_ff_12_q, t_ff_13_q, t_ff_14_q);
  or or_6 (or_6_out, and_15_out, and_17_out);
  not not_2 (not_2_out, 1'b1);
  or or_7 (or_7_out, t_ff_8_qn, t_ff_9_qn);
  and and_16 (and_16_out, t_ff_8_qn, t_ff_10_q);
  and and_17 (and_17_out, t_ff_11_q, t_ff_12_qn, t_ff_13_qn, t_ff_14_q);
  and and_18 (and_18_out, t_ff_11_qn, t_ff_13_q, t_ff_14_q);
  and and_19 (and_19_out, t_ff_11_qn, t_ff_14_q);
  or or_8 (or_8_out, t_ff_11_qn, and_20_out);
  and and_20 (and_20_out, t_ff_12_qn, t_ff_13_qn);
  // _7_segment_display_driver 7_segment_display_driver_3: pin names not known; wires that end beside it: t_ff_8_qn, t_ff_9_qn, t_ff_10_qn, not_2_out, t_ff_8_q, t_ff_9_q, t_ff_10_q, n7_segment_display_driver_3_p8, n7_segment_display_driver_3_p9, n7_segment_display_driver_3_p10, n7_segment_display_driver_3_p11, n7_segment_display_driver_3_p12, n7_segment_display_driver_3_p13, n7_segment_display_driver_3_p14
  // _7_segment_display_driver 7_segment_display_driver_4: pin names not known; wires that end beside it: t_ff_14_qn, t_ff_11_q, t_ff_12_q, t_ff_13_q, t_ff_14_q, n7_segment_display_driver_4_p6, n7_segment_display_driver_4_p7, n7_segment_display_driver_4_p8, n7_segment_display_driver_4_p9, n7_segment_display_driver_4_p10, n7_segment_display_driver_4_p11, n7_segment_display_driver_4_p12
  _7_Segment_Display u_7_segment_display_3 (
    .g(n7_segment_display_driver_3_p14), .f(n7_segment_display_driver_3_p13),
    .a(n7_segment_display_driver_3_p8), .b(n7_segment_display_driver_3_p9),
    .e(n7_segment_display_driver_3_p12), .d(n7_segment_display_driver_3_p11),
    .c(n7_segment_display_driver_3_p10));  // open: dp
  _7_Segment_Display u_7_segment_display_4 (
    .g(n7_segment_display_driver_4_p12), .f(n7_segment_display_driver_4_p11),
    .a(n7_segment_display_driver_4_p6), .b(n7_segment_display_driver_4_p7),
    .e(n7_segment_display_driver_4_p10), .d(n7_segment_display_driver_4_p9),
    .c(n7_segment_display_driver_4_p8));  // open: dp
endmodule
