// Logisim project Clock5.circ as structural Verilog: 1 circuit, main circuit main
module main (
);

  wire and_1_out, and_2_out, and_3_out, and_4_out, and_5_out, and_6_out, and_7_out, and_8_out, and_9_out,
       and_10_out, and_11_out, and_12_out, and_13_out, and_14_out, and_15_out, and_16_out, and_17_out,
       and_18_out, and_19_out, and_20_out, and_21_out, and_22_out, and_23_out, and_24_out, and_25_out,
       and_26_out, and_27_out, and_28_out, and_29_out, and_30_out, and_31_out, and_32_out, and_33_out,
       and_34_out, and_35_out, and_36_out, and_37_out, and_38_out, and_39_out, and_40_out, and_41_out,
       and_42_out, and_43_out, and_44_out, and_45_out, and_46_out, button_1_out, clock_1_out,
       n7_segment_display_driver_1_p5, n7_segment_display_driver_1_p6, n7_segment_display_driver_1_p7,
       n7_segment_display_driver_1_p8, n7_segment_display_driver_1_p9, n7_segment_display_driver_1_p10,
       n7_segment_display_driver_1_p11, n7_segment_display_driver_2_p5, n7_segment_display_driver_2_p6,
       n7_segment_display_driver_2_p7, n7_segment_display_driver_2_p8, n7_segment_display_driver_2_p9,
       n7_segment_display_driver_2_p10, n7_segment_display_driver_2_p11, n7_segment_display_driver_3_p5,
       n7_segment_display_driver_3_p6, n7_segment_display_driver_3_p7, n7_segment_display_driver_3_p8,
       n7_segment_display_driver_3_p9, n7_segment_display_driver_3_p10, n7_segment_display_driver_3_p11,
       n7_segment_display_driver_4_p5, n7_segment_display_driver_4_p6, n7_segment_display_driver_4_p7,
       n7_segment_display_driver_4_p8, n7_segment_display_driver_4_p9, n7_segment_display_driver_4_p10,
       n7_segment_display_driver_4_p11, n7_segment_display_driver_5_p5, n7_segment_display_driver_5_p6,
       n7_segment_display_driver_5_p7, n7_segment_display_driver_5_p8, n7_segment_display_driver_5_p9,
       n7_segment_display_driver_5_p10, n7_segment_display_driver_5_p11, n7_segment_display_driver_6_p5,
       n7_segment_display_driver_6_p6, n7_segment_display_driver_6_p7, n7_segment_display_driver_6_p8,
       n7_segment_display_driver_6_p9, n7_segment_display_driver_6_p10, n7_segment_display_driver_6_p11,
       nor_1_out, nor_2_out, not_1_out, not_2_out, not_3_out, or_1_out, or_2_out, or_3_out, or_4_out,
       or_5_out, or_6_out, or_7_out, or_8_out, or_9_out, or_10_out, or_11_out, or_12_out, or_13_out,
       or_14_out, or_15_out, t_ff_1_q, t_ff_1_qn, t_ff_2_q, t_ff_2_qn, t_ff_3_q, t_ff_3_qn, t_ff_4_q,
       t_ff_4_qn, t_ff_5_q, t_ff_5_qn, t_ff_6_q, t_ff_6_qn, t_ff_7_q, t_ff_8_q, t_ff_8_qn, t_ff_9_q,
       t_ff_9_qn, t_ff_10_q, t_ff_10_qn, t_ff_11_q, t_ff_12_q, t_ff_13_q, t_ff_13_qn, t_ff_14_q, t_ff_14_qn,
       t_ff_15_q, t_ff_16_q, t_ff_16_qn, t_ff_17_q, t_ff_17_qn, t_ff_18_q, t_ff_18_qn, t_ff_19_q;

  T_Flip_Flop #(.trigger("falling")) t_ff_1 (
    .clk(and_23_out), .T(or_4_out), .Q(t_ff_1_q), .Qn(t_ff_1_qn), .en(1'b1));  // open: preset, reset
  T_Flip_Flop #(.trigger("falling")) t_ff_2 (
    .clk(and_23_out), .T(or_3_out), .Q(t_ff_2_q), .Qn(t_ff_2_qn), .en(1'b1));  // open: preset, reset
  T_Flip_Flop #(.trigger("falling")) t_ff_3 (
    .clk(and_23_out), .T(or_2_out), .Q(t_ff_3_q), .Qn(t_ff_3_qn), .en(1'b1));  // open: preset, reset
  T_Flip_Flop #(.trigger("falling")) t_ff_4 (
    .clk(and_23_out), .T(or_1_out), .Q(t_ff_4_q), .Qn(t_ff_4_qn), .preset(button_1_out), .en(1'b1));  // open: reset
  and and_1 (and_1_out, t_ff_1_qn, t_ff_4_q);
  and and_2 (and_2_out, t_ff_1_qn, t_ff_3_q);
  and and_3 (and_3_out, t_ff_1_q, t_ff_2_qn);
  and and_4 (and_4_out, t_ff_2_q, t_ff_3_qn, t_ff_4_qn);
  or or_1 (or_1_out, and_1_out, and_2_out, and_3_out, and_4_out);
  and and_5 (and_5_out, t_ff_2_qn, t_ff_4_q);
  and and_6 (and_6_out, t_ff_1_qn, t_ff_4_q);
  or or_2 (or_2_out, and_6_out, and_5_out);
  and and_7 (and_7_out, t_ff_1_q, t_ff_2_qn);
  and and_8 (and_8_out, t_ff_3_q, t_ff_4_q);
  and and_9 (and_9_out, t_ff_2_qn, t_ff_3_q, t_ff_4_q);
  and and_10 (and_10_out, t_ff_1_qn, t_ff_3_q, t_ff_4_q);
  or or_3 (or_3_out, and_10_out, and_9_out, and_13_out);
  and and_11 (and_11_out, and_7_out, and_8_out);
  and and_12 (and_12_out, t_ff_1_qn, t_ff_2_q, t_ff_3_q, t_ff_4_q);
  and and_13 (and_13_out, t_ff_1_q, t_ff_2_q, t_ff_3_qn, t_ff_4_qn);
  or or_4 (or_4_out, and_12_out, and_13_out);
  and and_14 (and_14_out, t_ff_1_qn, t_ff_2_q);
  and and_15 (and_15_out, t_ff_1_q, t_ff_2_q);
  and and_16 (and_16_out, t_ff_3_qn, t_ff_4_qn);
  and and_17 (and_17_out, t_ff_1_qn, t_ff_3_q);
  and and_18 (and_18_out, t_ff_1_qn, t_ff_4_q);
  and and_19 (and_19_out, t_ff_2_qn, t_ff_4_q);
  or or_5 (or_5_out, and_22_out, and_20_out);
  and and_20 (and_20_out, t_ff_1_q, t_ff_2_qn, t_ff_3_q);
  and and_21 (and_21_out, t_ff_1_q, t_ff_2_qn, t_ff_3_qn);
  and and_22 (and_22_out, and_15_out, and_16_out);
  or or_6 (or_6_out, and_22_out, and_17_out);
  or or_7 (or_7_out, and_18_out, and_19_out);
  not not_1 (not_1_out, 1'b1);
  and and_23 (and_23_out, and_24_out, and_27_out);
  // _7_segment_display_driver 7_segment_display_driver_1: pin names not known; wires that end beside it: not_1_out, not_1_out, not_1_out, or_5_out, n7_segment_display_driver_1_p5, n7_segment_display_driver_1_p6, n7_segment_display_driver_1_p7, n7_segment_display_driver_1_p8, n7_segment_display_driver_1_p9, n7_segment_display_driver_1_p10, n7_segment_display_driver_1_p11
  // _7_segment_display_driver 7_segment_display_driver_2: pin names not known; wires that end beside it: and_21_out, and_14_out, or_6_out, or_7_out, n7_segment_display_driver_2_p5, n7_segment_display_driver_2_p6, n7_segment_display_driver_2_p7, n7_segment_display_driver_2_p8, n7_segment_display_driver_2_p9, n7_segment_display_driver_2_p10, n7_segment_display_driver_2_p11
  and and_24 (and_24_out, t_ff_5_q, t_ff_6_qn, t_ff_7_q);
  and and_25 (and_25_out, and_23_out, and_35_out, and_11_out);
  T_Flip_Flop #(.trigger("falling")) t_ff_5 (
    .clk(and_27_out), .T(or_8_out), .Q(t_ff_5_q), .Qn(t_ff_5_qn), .en(1'b1));  // open: preset, reset
  T_Flip_Flop #(.trigger("falling")) t_ff_6 (
    .clk(and_27_out), .T(and_30_out), .Q(t_ff_6_q), .Qn(t_ff_6_qn), .en(1'b1));  // open: preset, reset
  T_Flip_Flop #(.trigger("falling")) t_ff_7 (
    .clk(and_27_out), .T(or_10_out), .Q(t_ff_7_q), .en(1'b1));  // open: Qn, preset, reset
  and and_26 (and_26_out, t_ff_5_q, t_ff_6_qn, t_ff_7_q);
  or or_8 (or_8_out, and_26_out, and_29_out);
  and and_27 (and_27_out, t_ff_11_q, t_ff_10_qn, t_ff_9_qn, t_ff_8_q);
  T_Flip_Flop #(.trigger("falling")) t_ff_8 (
    .clk(and_35_out), .T(or_9_out), .Q(t_ff_8_q), .Qn(t_ff_8_qn), .en(1'b1));  // open: preset, reset
  T_Flip_Flop #(.trigger("falling")) t_ff_9 (
    .clk(and_35_out), .T(and_33_out), .Q(t_ff_9_q), .Qn(t_ff_9_qn), .en(1'b1));  // open: preset, reset
  T_Flip_Flop #(.trigger("falling")) t_ff_10 (
    .clk(and_35_out), .T(and_32_out), .Q(t_ff_10_q), .Qn(t_ff_10_qn), .en(1'b1));  // open: preset, reset
  T_Flip_Flop #(.trigger("falling")) t_ff_11 (
    .clk(and_35_out), .T(or_11_out), .Q(t_ff_11_q), .en(1'b1));  // open: Qn, preset, reset
  and and_28 (and_28_out, t_ff_8_qn, t_ff_9_q, t_ff_10_q, t_ff_11_q);
  and and_29 (and_29_out, t_ff_5_qn, t_ff_6_q, t_ff_7_q);
  and and_30 (and_30_out, t_ff_5_qn, t_ff_7_q);
  and and_31 (and_31_out, t_ff_8_q, t_ff_9_qn, t_ff_10_qn, t_ff_11_q);
  or or_9 (or_9_out, and_28_out, and_31_out);
  not not_2 (not_2_out, 1'b1);
  or or_10 (or_10_out, t_ff_5_qn, t_ff_6_qn);
  and and_32 (and_32_out, t_ff_8_qn, t_ff_11_q);
  and and_33 (and_33_out, t_ff_8_qn, t_ff_10_q, t_ff_11_q);
  _7_Segment_Display u_7_segment_display_1 (
    .g(n7_segment_display_driver_2_p11), .f(n7_segment_display_driver_2_p10),
    .a(n7_segment_display_driver_2_p5), .b(n7_segment_display_driver_2_p6),
    .e(n7_segment_display_driver_2_p9), .d(n7_segment_display_driver_2_p8), .c(n7_segment_display_driver_2_p7));  // open: dp
  _7_Segment_Display u_7_segment_display_2 (
    .g(n7_segment_display_driver_1_p11), .f(n7_segment_display_driver_1_p10),
    .a(n7_segment_display_driver_1_p5), .b(n7_segment_display_driver_1_p6),
    .e(n7_segment_display_driver_1_p9), .d(n7_segment_display_driver_1_p8), .c(n7_segment_display_driver_1_p7));  // open: dp
  and and_34 (and_34_out, t_ff_9_qn, t_ff_10_qn);
  or or_11 (or_11_out, t_ff_8_qn, and_34_out);
  // _7_segment_display_driver 7_segment_display_driver_3: pin names not known; wires that end beside it: t_ff_8_q, t_ff_9_q, t_ff_10_q, t_ff_11_q, n7_segment_display_driver_3_p5, n7_segment_display_driver_3_p6, n7_segment_display_driver_3_p7, n7_segment_display_driver_3_p8, n7_segment_display_driver_3_p9, n7_segment_display_driver_3_p10, n7_segment_display_driver_3_p11
  // _7_segment_display_driver 7_segment_display_driver_4: pin names not known; wires that end beside it: not_2_out, t_ff_5_q, t_ff_6_q, t_ff_7_q, n7_segment_display_driver_4_p5, n7_segment_display_driver_4_p6, n7_segment_display_driver_4_p7, n7_segment_display_driver_4_p8, n7_segment_display_driver_4_p9, n7_segment_display_driver_4_p10, n7_segment_display_driver_4_p11
  T_Flip_Flop #(.trigger("falling")) t_ff_12 (
    .clk(and_25_out), .T(1'b1), .Q(t_ff_12_q), .en(1'b1));  // open: Qn, preset, reset
  _7_Segment_Display u_7_segment_display_3 (
    .g(n7_segment_display_driver_4_p11), .f(n7_segment_display_driver_4_p10),
    .a(n7_segment_display_driver_4_p5), .b(n7_segment_display_driver_4_p6),
    .e(n7_segment_display_driver_4_p9), .d(n7_segment_display_driver_4_p8), .c(n7_segment_display_driver_4_p7));  // open: dp
  _7_Segment_Display u_7_segment_display_4 (
    .g(1'b1), .f(1'b1), .a(1'b1), .b(1'b1), .e(1'b1), .c(t_ff_12_q));  // open: d, dp
  _7_Segment_Display u_7_segment_display_5 (
    .g(n7_segment_display_driver_3_p11), .f(n7_segment_display_driver_3_p10),
    .a(n7_segment_display_driver_3_p5), .b(n7_segment_display_driver_3_p6),
    .e(n7_segment_display_driver_3_p9), .d(n7_segment_display_driver_3_p8), .c(n7_segment_display_driver_3_p7));  // open: dp
  Button button_1 (.out(button_1_out));
  _7_Segment_Display u_7_segment_display_6 (
    .g(n7_segment_display_driver_5_p11), .f(n7_segment_display_driver_5_p10),
    .a(n7_segment_display_driver_5_p5), .b(n7_segment_display_driver_5_p6),
    .e(n7_segment_display_driver_5_p9), .d(n7_segment_display_driver_5_p8), .c(n7_segment_display_driver_5_p7));  // open: dp
  Clock clock_1 (.out(clock_1_out));
  _7_Segment_Display u_7_segment_display_7 (
    .g(n7_segment_display_driver_6_p11), .f(n7_segment_display_driver_6_p10),
    .a(n7_segment_display_driver_6_p5), .b(n7_segment_display_driver_6_p6),
    .e(n7_segment_display_driver_6_p9), .d(n7_segment_display_driver_6_p8), .c(n7_segment_display_driver_6_p7));  // open: dp
  and and_35 (and_35_out, and_37_out, and_38_out);
  nor nor_1 (nor_1_out, 1'b0, nor_2_out);
  nor nor_2 (nor_2_out, nor_1_out, button_1_out);
  and and_36 (and_36_out, nor_1_out, clock_1_out);
  and and_37 (and_37_out, t_ff_15_q, t_ff_14_qn, t_ff_13_q);
  T_Flip_Flop #(.trigger("falling")) t_ff_13 (
    .clk(and_38_out), .T(or_12_out), .Q(t_ff_13_q), .Qn(t_ff_13_qn), .en(1'b1));  // open: preset, reset
  T_Flip_Flop #(.trigger("falling")) t_ff_14 (
    .clk(and_38_out), .T(and_42_out), .Q(t_ff_14_q), .Qn(t_ff_14_qn), .en(1'b1));  // open: preset, reset
  T_Flip_Flop #(.trigger("falling")) t_ff_15 (
    .clk(and_38_out), .T(or_14_out), .Q(t_ff_15_q), .en(1'b1));  // open: Qn, preset, reset
  and and_38 (and_38_out, t_ff_19_q, t_ff_18_qn, t_ff_17_qn, t_ff_16_q);
  T_Flip_Flop #(.trigger("falling")) t_ff_16 (
    .clk(and_36_out), .T(or_13_out), .Q(t_ff_16_q), .Qn(t_ff_16_qn), .en(1'b1));  // open: preset, reset
  T_Flip_Flop #(.trigger("falling")) t_ff_17 (
    .clk(and_36_out), .T(and_45_out), .Q(t_ff_17_q), .Qn(t_ff_17_qn), .en(1'b1));  // open: preset, reset
  T_Flip_Flop #(.trigger("falling")) t_ff_18 (
    .clk(and_36_out), .T(and_44_out), .Q(t_ff_18_q), .Qn(t_ff_18_qn), .en(1'b1));  // open: preset, reset
  T_Flip_Flop #(.trigger("falling")) t_ff_19 (
    .clk(and_36_out), .T(or_15_out), .Q(t_ff_19_q), .en(1'b1));  // open: Qn, preset, reset
  and and_39 (and_39_out, t_ff_13_qn, t_ff_14_q, t_ff_15_q);
  and and_40 (and_40_out, t_ff_13_q, t_ff_14_qn, t_ff_15_q);
  or or_12 (or_12_out, and_40_out, and_39_out);
  and and_41 (and_41_out, t_ff_16_qn, t_ff_17_q, t_ff_18_q, t_ff_19_q);
  and and_42 (and_42_out, t_ff_13_qn, t_ff_15_q);
  and and_43 (and_43_out, t_ff_16_q, t_ff_17_qn, t_ff_18_qn, t_ff_19_q);
  or or_13 (or_13_out, and_41_out, and_43_out);
  not not_3 (not_3_out, 1'b1);
  or or_14 (or_14_out, t_ff_13_qn, t_ff_14_qn);
  and and_44 (and_44_out, t_ff_16_qn, t_ff_19_q);
  and and_45 (and_45_out, t_ff_16_qn, t_ff_18_q, t_ff_19_q);
  // _7_segment_display_driver 7_segment_display_driver_5: pin names not known; wires that end beside it: not_3_out, t_ff_13_q, t_ff_14_q, t_ff_15_q, n7_segment_display_driver_5_p5, n7_segment_display_driver_5_p6, n7_segment_display_driver_5_p7, n7_segment_display_driver_5_p8, n7_segment_display_driver_5_p9, n7_segment_display_driver_5_p10, n7_segment_display_driver_5_p11
  and and_46 (and_46_out, t_ff_17_qn, t_ff_18_qn);
  or or_15 (or_15_out, t_ff_16_qn, and_46_out);
  // _7_segment_display_driver 7_segment_display_driver_6: pin names not known; wires that end beside it: t_ff_16_q, t_ff_17_q, t_ff_18_q, t_ff_19_q, n7_segment_display_driver_6_p5, n7_segment_display_driver_6_p6, n7_segment_display_driver_6_p7, n7_segment_display_driver_6_p8, n7_segment_display_driver_6_p9, n7_segment_display_driver_6_p10, n7_segment_display_driver_6_p11

  // Notes on the sheet:
  //   Press to turn on the clock
endmodule
